// Logisim project cl2e1_starter.circ as structural Verilog: 1 circuit, main circuit main
module main (
  input  _1,
  input  _2,
  input  _3,
  output Output
);

  wire and_1_out, and_2_out, and_3_out, not_1_out, not_2_out, not_3_out, not_4_out, not_5_out, not_6_out;

  not not_1 (not_1_out, _2);
  not not_2 (not_2_out, _3);
  not not_3 (not_3_out, _1);
  not not_4 (not_4_out, _3);
  not not_5 (not_5_out, _1);
  not not_6 (not_6_out, _2);
  and and_1 (and_1_out, not_1_out, _1, not_2_out);
  and and_2 (and_2_out, _2, _2, not_3_out, not_4_out);
  and and_3 (and_3_out, not_5_out, not_6_out, _3);
  or or_1 (Output, and_1_out, and_2_out, and_3_out);

  // Notes on the sheet:
  //   Inputs
endmodule
