// Logisim project cl2e3_starter.circ as structural Verilog: 1 circuit, main circuit main
module main (
  input  [3:0] in_1,
  input  in_2,
  output Output
);

  wire decoder_1_out4, decoder_1_out5, decoder_1_out7, decoder_1_out12, decoder_1_out13;

  Decoder #(.select(4)) decoder_1 (
    .out4(decoder_1_out4), .out5(decoder_1_out5), .out7(decoder_1_out7), .out12(decoder_1_out12),
    .out13(decoder_1_out13), .sel(in_1), .en(in_2));  // open: out0, out1, out2, out3, out6, out8, out9, out10, out11, out14, out15
  or or_1 (Output, decoder_1_out4, decoder_1_out5, decoder_1_out7, decoder_1_out12, decoder_1_out13);

  // Notes on the sheet:
  //   Inputs
endmodule
