// Logisim project counters_starter-p3.circ as structural Verilog: 1 circuit, main circuit main
module main (
  input  in_1,
  output [3:0] Outputs
);

  wire and_1_out, and_2_out, and_3_out, and_4_out, and_5_out, and_6_out, and_7_out, and_8_out, and_9_out,
       and_10_out, and_11_out, and_12_out, and_13_out, and_14_out, and_15_out, and_16_out, and_17_out,
       and_18_out, and_19_out, and_20_out, and_21_out, and_22_out, clock_1_out, d_ff_1_qn, d_ff_2_qn,
       d_ff_3_qn, d_ff_4_qn, not_1_out, or_1_out, or_2_out, or_3_out, or_4_out, or_5_out, or_6_out, or_7_out,
       or_8_out, or_9_out;

  Clock clock_1 (.out(clock_1_out));
  or or_1 (or_1_out, and_1_out, and_4_out);
  or or_2 (or_2_out, and_2_out, and_5_out);
  or or_3 (or_3_out, and_3_out, and_6_out);
  not not_1 (not_1_out, in_1);
  D_Flip_Flop #(.trigger("falling")) d_ff_1 (
    .clk(clock_1_out), .D(or_3_out), .Q(Outputs[3]), .Qn(d_ff_1_qn));  // open: preset, en, reset
  D_Flip_Flop #(.trigger("falling")) d_ff_2 (
    .clk(clock_1_out), .D(or_2_out), .Q(Outputs[2]), .Qn(d_ff_2_qn));  // open: preset, en, reset
  D_Flip_Flop #(.trigger("falling")) d_ff_3 (
    .clk(clock_1_out), .D(or_1_out), .Q(Outputs[1]), .Qn(d_ff_3_qn));  // open: preset, en, reset
  D_Flip_Flop #(.trigger("falling")) d_ff_4 (
    .clk(clock_1_out), .D(d_ff_4_qn), .Q(Outputs[0]), .Qn(d_ff_4_qn));  // open: preset, en, reset
  and and_1 (and_1_out, or_4_out, in_1);
  and and_2 (and_2_out, or_5_out, in_1);
  and and_3 (and_3_out, or_6_out, in_1);
  or or_4 (or_4_out, and_7_out, and_9_out);
  or or_5 (or_5_out, and_8_out, and_10_out, and_11_out);
  or or_6 (or_6_out, and_12_out, and_13_out, and_14_out);
  and and_4 (and_4_out, or_7_out, not_1_out);
  and and_5 (and_5_out, or_8_out, not_1_out);
  and and_6 (and_6_out, or_9_out, not_1_out);
  and and_7 (and_7_out, d_ff_3_qn, d_ff_4_qn);
  and and_8 (and_8_out, Outputs[2], d_ff_3_qn);
  and and_9 (and_9_out, d_ff_1_qn, d_ff_2_qn);
  or or_7 (or_7_out, and_15_out, and_17_out);
  or or_8 (or_8_out, and_16_out, and_18_out);
  or or_9 (or_9_out, and_19_out, and_21_out);
  and and_10 (and_10_out, Outputs[3], d_ff_2_qn);
  and and_11 (and_11_out, d_ff_1_qn, Outputs[0]);
  and and_12 (and_12_out, Outputs[2], d_ff_3_qn);
  and and_13 (and_13_out, d_ff_3_qn, Outputs[0]);
  and and_14 (and_14_out, Outputs[1], d_ff_4_qn);
  and and_15 (and_15_out, d_ff_2_qn, d_ff_3_qn, d_ff_3_qn);
  and and_16 (and_16_out, d_ff_2_qn, d_ff_3_qn);
  and and_17 (and_17_out, d_ff_1_qn, d_ff_4_qn);
  and and_18 (and_18_out, Outputs[3], Outputs[0], Outputs[0]);
  and and_19 (and_19_out, d_ff_4_qn, d_ff_3_qn);
  and and_20 (and_20_out, d_ff_3_qn, Outputs[0]);
  and and_21 (and_21_out, Outputs[3], Outputs[2]);
  and and_22 (and_22_out, Outputs[1], Outputs[1], d_ff_4_qn);
endmodule
