// Logisim project inclassexcercise2.circ as structural Verilog: 1 circuit, main circuit main
module main (
  input  in_1
);

  wire and_1_out, and_2_out, and_3_out, and_4_out, clock_1_out, d_ff_1_q, d_ff_1_qn, d_ff_2_q, d_ff_2_qn,
       d_ff_3_q, d_ff_3_qn, not_1_out;

  Clock clock_1 (.out(clock_1_out));
  D_Flip_Flop d_ff_1 (.clk(clock_1_out), .Q(d_ff_1_q), .Qn(d_ff_1_qn));  // open: D, preset, en, reset
  D_Flip_Flop d_ff_2 (.clk(clock_1_out), .Q(d_ff_2_q), .Qn(d_ff_2_qn));  // open: D, preset, en, reset
  D_Flip_Flop d_ff_3 (.clk(clock_1_out), .Q(d_ff_3_q), .Qn(d_ff_3_qn));  // open: D, preset, en, reset
  // OR_Gate or_1 has open pins: in0=and_1_out, in1=and_2_out, in2=and_3_out, in3=and_4_out, out=open
  not not_1 (not_1_out, in_1);
  and and_1 (and_1_out, d_ff_1_q, d_ff_2_qn);
  and and_2 (and_2_out, d_ff_1_q, d_ff_3_qn, not_1_out);
  and and_3 (and_3_out, d_ff_1_qn, d_ff_2_q, in_1);
  buf and_4 (and_4_out, d_ff_1_qn);  // AND_Gate
endmodule
