// Logisim project sle1_starter.circ as structural Verilog: 1 circuit, main circuit main
module main (
  input  S,
  input  R,
  output Q,
  output Q_prime
);

  wire nor_1_out, nor_2_out;

  nor nor_1 (nor_1_out, S, nor_2_out);
  nor nor_2 (nor_2_out, nor_1_out, R);
  not not_1 (Q, nor_1_out);
  not not_2 (Q_prime, nor_2_out);

  // Notes on the sheet:
  //   Inputs
  //   Outputs
endmodule
