// Logisim project sle2_starter.circ as structural Verilog: 1 circuit, main circuit main
module main (
  input  in_1,
  output Output
);

  wire and_1_out, and_2_out, and_3_out, and_4_out, and_5_out, and_6_out, and_7_out, and_8_out, clock_1_out,
       d_ff_1_q, d_ff_1_qn, d_ff_2_q, d_ff_2_qn, not_1_out, or_1_out, or_2_out;

  Clock clock_1 (.out(clock_1_out));
  or or_1 (or_1_out, and_3_out, and_2_out, and_1_out);
  or or_2 (or_2_out, and_7_out, and_8_out, and_6_out, and_5_out, and_4_out);
  D_Flip_Flop #(.trigger("falling")) d_ff_1 (
    .clk(clock_1_out), .D(or_1_out), .Q(d_ff_1_q), .Qn(d_ff_1_qn));  // open: preset, en, reset
  D_Flip_Flop #(.trigger("falling")) d_ff_2 (
    .clk(clock_1_out), .D(or_2_out), .Q(d_ff_2_q), .Qn(d_ff_2_qn));  // open: preset, en, reset
  not not_1 (not_1_out, in_1);
  and and_1 (and_1_out, d_ff_1_qn, d_ff_2_q, in_1);
  and and_2 (and_2_out, d_ff_1_q, d_ff_2_qn, not_1_out);
  and and_3 (and_3_out, d_ff_1_q, d_ff_2_q, not_1_out);
  and and_4 (and_4_out, d_ff_1_qn, d_ff_2_qn, in_1);
  and and_5 (and_5_out, d_ff_1_qn, d_ff_2_q, not_1_out);
  and and_6 (and_6_out, d_ff_1_qn, d_ff_2_q, in_1);
  and and_7 (and_7_out, d_ff_1_q, d_ff_2_q, not_1_out);
  and and_8 (and_8_out, d_ff_1_q, d_ff_2_qn, in_1);
  and and_9 (Output, d_ff_1_q, d_ff_2_q);

  // Notes on the sheet:
  //   Input
endmodule
