// Logisim project sle4_starter.circ as structural Verilog: 1 circuit, main circuit main
module main (
  input  in_1,
  output [3:0] Outputs
);

  wire and_1_out, and_2_out, and_3_out, and_4_out, and_5_out, and_6_out, and_7_out, and_8_out, and_9_out,
       and_10_out, and_11_out, and_12_out, and_13_out, clock_1_out, d_ff_1_qn, d_ff_2_qn, d_ff_3_qn,
       d_ff_4_qn, not_1_out, or_1_out, or_2_out, or_3_out;

  Clock clock_1 (.out(clock_1_out));
  and and_1 (and_1_out, or_1_out, not_1_out);
  and and_2 (and_2_out, or_2_out, not_1_out);
  and and_3 (and_3_out, or_3_out, not_1_out);
  not not_1 (not_1_out, in_1);
  D_Flip_Flop #(.trigger("falling")) d_ff_1 (
    .clk(clock_1_out), .D(and_3_out), .Q(Outputs[3]), .Qn(d_ff_1_qn));  // open: preset, en, reset
  D_Flip_Flop #(.trigger("falling")) d_ff_2 (
    .clk(clock_1_out), .D(and_2_out), .Q(Outputs[2]), .Qn(d_ff_2_qn));  // open: preset, en, reset
  D_Flip_Flop #(.trigger("falling")) d_ff_3 (
    .clk(clock_1_out), .D(and_1_out), .Q(Outputs[1]), .Qn(d_ff_3_qn));  // open: preset, en, reset
  D_Flip_Flop #(.trigger("falling")) d_ff_4 (
    .clk(clock_1_out), .D(and_4_out), .Q(Outputs[0]), .Qn(d_ff_4_qn));  // open: preset, en, reset
  and and_4 (and_4_out, d_ff_4_qn, not_1_out);
  or or_1 (or_1_out, and_5_out, and_6_out);
  or or_2 (or_2_out, and_8_out, and_7_out, and_9_out);
  or or_3 (or_3_out, and_10_out, and_11_out, and_12_out, and_13_out);
  and and_5 (and_5_out, d_ff_3_qn, Outputs[0]);
  and and_6 (and_6_out, Outputs[1], d_ff_4_qn);
  and and_7 (and_7_out, Outputs[2], d_ff_4_qn);
  and and_8 (and_8_out, Outputs[2], d_ff_3_qn);
  and and_9 (and_9_out, d_ff_2_qn, Outputs[1], Outputs[1], Outputs[0]);
  and and_10 (and_10_out, Outputs[3], d_ff_3_qn);
  and and_11 (and_11_out, Outputs[3], d_ff_2_qn);
  and and_12 (and_12_out, Outputs[3], d_ff_4_qn);
  and and_13 (and_13_out, d_ff_1_qn, Outputs[2], Outputs[1], Outputs[0]);
endmodule
