// Logisim project slexcercise1.circ as structural Verilog: 1 circuit, main circuit main
module main (
  output out_1,
  output out_2,
  output out_3,
  output out_4
);

  wire and_1_out, and_2_out, and_3_out, and_4_out, and_5_out, and_6_out, and_7_out, and_8_out, and_9_out,
       clock_1_out, d_ff_2_q, d_ff_2_qn, d_ff_3_q, d_ff_3_qn, or_1_out, or_2_out;

  Clock clock_1 (.out(clock_1_out));
  or or_1 (or_1_out, and_1_out, and_2_out);
  or or_2 (or_2_out, and_3_out, and_4_out, and_5_out);
  D_Flip_Flop #(.trigger("falling")) d_ff_1 (
    .clk(clock_1_out), .D(or_2_out), .Q(out_3), .Qn(out_4));  // open: preset, en, reset
  D_Flip_Flop #(.trigger("falling")) d_ff_2 (
    .clk(clock_1_out), .D(or_1_out), .Q(d_ff_2_q), .Qn(d_ff_2_qn));  // open: preset, en, reset
  D_Flip_Flop #(.trigger("falling")) d_ff_3 (
    .clk(clock_1_out), .D(d_ff_3_qn), .Q(d_ff_3_q), .Qn(d_ff_3_qn));  // open: preset, en, reset
  and and_1 (and_1_out, d_ff_2_q, d_ff_3_qn);
  and and_2 (and_2_out, d_ff_2_qn, d_ff_3_q);
  and and_3 (and_3_out, out_3, d_ff_3_qn);
  and and_4 (and_4_out, out_3, d_ff_2_qn);
  and and_5 (and_5_out, out_4, d_ff_2_q, d_ff_3_q);
  and and_6 (and_6_out, out_3, d_ff_2_qn);
  and and_7 (and_7_out, d_ff_2_q, out_4);
  and and_8 (and_8_out, out_3, d_ff_3_qn);
  and and_9 (and_9_out, out_4, d_ff_3_q);
  or or_3 (out_1, and_7_out, and_6_out);
  or or_4 (out_2, and_9_out, and_8_out);
endmodule
